# Fritzing sketch Base (saved by Fritzing 0.9.3b)
circuit board: 6.88566cm x 5.36311cm

parts:
  HC-05 = female pin header, 6 pins [form="♀ (female)"]
  Bauteil1 = Arduino Uno (Rev3)
  MCP2515_CAN = female pin header, 7 pins [form="♀ (female)"]
  Bauteil3 = Bluetooth HC-05 Macho  # not connected
  M2 = Niren can bus module [package=THT]  # not connected
  HC05VCC = female pin header, 3 pins [form="♀ (female)"]
  I2C = female pin header, 4 pins [form="♀ (female)"]
  FPL = female pin header, 4 pins [form="♀ (female)"]
  FPR = female pin header, 4 pins [form="♀ (female)"]
  ENCROT = female pin header, 4 pins [form="♀ (female)"]
  ENCFPR = female pin header, 4 pins [form="♀ (female)"]
  ENCFPL = female pin header, 4 pins [form="♀ (female)"]
  I2C1 = female pin header, 4 pins [form="♀ (female)"]
  2KOHM = Resistor [tolerance=±5% resistance=220 package=THT]
  1KOHM = Resistor [tolerance=±5% resistance=220 package=THT]

nets:
  N1: HC-05.pin2, 2KOHM.Pin_1, 1KOHM.Pin_1
  N2: HC-05.pin3, Bauteil1.D0/RX
  N3: HC-05.pin4, Bauteil1.GND, MCP2515_CAN.pin6, I2C.pin1, FPL.pin2, FPR.pin2, ENCROT.pin2, ENCFPR.pin2, ENCFPL.pin2, I2C1.pin1, 2KOHM.Pin_0
  N4: HC-05.pin5, HC05VCC.pin2
  N5: Bauteil1.A0, ENCFPL.pin3
  N6: Bauteil1.A1, ENCFPL.pin4
  N7: Bauteil1.A2, FPR.pin3
  N8: Bauteil1.A3, FPR.pin4
  N9: Bauteil1.A4/SDA, I2C.pin3, I2C1.pin3
  N10: Bauteil1.A5/SCL, I2C.pin4, I2C1.pin4
  N11: Bauteil1.D8, FPL.pin3
  N12: Bauteil1.D9_PWM, FPL.pin1
  N13: Bauteil1.D10_PWM/SS, MCP2515_CAN.pin5
  N14: Bauteil1.D11_PWM/MOSI, MCP2515_CAN.pin3
  N15: Bauteil1.D12/MISO, MCP2515_CAN.pin4
  N16: Bauteil1.D13/SCK, MCP2515_CAN.pin2
  N17: Bauteil1.D1/TX, 1KOHM.Pin_0
  N18: Bauteil1.D2, ENCROT.pin4
  N19: Bauteil1.D3_PWM, ENCROT.pin3
  N20: Bauteil1.D4, ENCFPR.pin4
  N21: Bauteil1.D5_PWM, ENCFPR.pin3
  N22: Bauteil1.D6_PWM, FPR.pin1
  N23: Bauteil1.D7, FPL.pin4
  N24: Bauteil1.3V3, HC05VCC.pin3
  N25: Bauteil1.5V, MCP2515_CAN.pin7, HC05VCC.pin1, I2C.pin2, ENCROT.pin1, ENCFPR.pin1, ENCFPL.pin1, I2C1.pin2

notes:
  GND
  5V
  SDA
  SCL
  3V
  PWM
  EN1
  EN2
  CHA
  CHB
  VCC
  RX
  TX
  CS
  S0
  SI
  SCK
  INT
  HC-05
  MCP2515_CAN

custom parts:
  Niren can bus module: Niren can bus module availabe on ebay and others. Pcb view assumes that you unsolder the 7 pin header and resolder it on the bottom of the module to connect to the pcb. The two jumpers and the can bus connector remain on the top of the board and don't appear in pcb view.
