# Fritzing sketch Arduino Shield (saved by Fritzing 0.9.3b)

parts:
  Part1 = Arduino Uno (Rev3) - ICSP
  RIGHT_FOOTPRINT = female pin header, 4 pins [form="♀ (female)"]
  SERVO-RIGHT = female pin header, 3 pins [form="♀ (female)"]
  SERVO-LEFT = female pin header, 3 pins [form="♀ (female)"]
  MOTOR1+2 = shrouded pin header, 12 pins [form="♂ (shrouded male)"]
  MOTOR3+4 = shrouded pin header, 12 pins [form="♂ (shrouded male)"]
  STEPPER2 = shrouded pin header, 12 pins [form="♂ (shrouded male)"]
  STEPPER1 = shrouded pin header, 12 pins [form="♂ (shrouded male)"]
  LEFT_FOOTPRINT = female pin header, 4 pins [form="♀ (female)"]
  ENCODER = female pin header, 4 pins [form="♀ (female)"]

nets:
  N1: Part1.A0, STEPPER2.pin2, STEPPER1.pin2
  N2: Part1.A3, RIGHT_FOOTPRINT.pin3, LEFT_FOOTPRINT.pin3
  N3: Part1.A4/SDA, RIGHT_FOOTPRINT.pin4, LEFT_FOOTPRINT.pin4
  N4: Part1.ICSP_MISO, Part1.D12/MISO, STEPPER2.pin4, STEPPER1.pin4
  N5: Part1.D8, MOTOR1+2.pin2, MOTOR1+2.pin4, MOTOR3+4.pin2, MOTOR3+4.pin4
  N6: Part1.D9_PWM, SERVO-LEFT.pin3
  N7: Part1.D10_PWM/SS, SERVO-RIGHT.pin3
  N8: Part1.D11_PWM/MOSI, STEPPER2.pin5, STEPPER1.pin5
  N9: Part1.D13/SCK, STEPPER2.pin3, STEPPER1.pin3
  N10: Part1.GND, RIGHT_FOOTPRINT.pin2, SERVO-RIGHT.pin1, SERVO-LEFT.pin1, LEFT_FOOTPRINT.pin2, ENCODER.pin1
  N11: Part1.D2, ENCODER.pin4
  N12: Part1.D3_PWM, ENCODER.pin3
  N13: Part1.D6_PWM, MOTOR1+2.pin1, MOTOR1+2.pin6, MOTOR3+4.pin1, MOTOR3+4.pin6
  N14: Part1.D7, MOTOR1+2.pin3, MOTOR1+2.pin5, MOTOR3+4.pin3, MOTOR3+4.pin5
  N15: Part1.5V, RIGHT_FOOTPRINT.pin1, LEFT_FOOTPRINT.pin1, ENCODER.pin2
  N16: SERVO-RIGHT.pin2, STEPPER1.pin6, STEPPER1.pin7
  N17: SERVO-LEFT.pin2, STEPPER2.pin1, STEPPER2.pin12
  N18: STEPPER2.pin6, STEPPER2.pin7
  N19: STEPPER1.pin1, STEPPER1.pin12
