# Fritzing sketch Footplate (saved by Fritzing 0.9.3b)
circuit board: 5.59999cm x 15.8cm

parts:
  VL6180X-B2 = Adafruit VL6180X Time of Flight Distance Sensor [part_number="Adafruit #3316"]
  VL6180X-T5 = Adafruit VL6180X Time of Flight Distance Sensor [part_number="Adafruit #3316"]
  VL6180X-T1 = Adafruit VL6180X Time of Flight Distance Sensor [part_number="Adafruit #3316"]
  VL6180X-B5 = Adafruit VL6180X Time of Flight Distance Sensor [part_number="Adafruit #3316"]
  VL6180X-B1 = Adafruit VL6180X Time of Flight Distance Sensor [part_number="Adafruit #3316"]
  VL6180X-T2 = Adafruit VL6180X Time of Flight Distance Sensor [part_number="Adafruit #3316"]
  GY271-T0 = Boladge HMC5883L Compass Module
  TCA9548A-T = Adafruit TCA9548A
  TCA9548A-B = Adafruit TCA9548A
  GY271-B0 = Boladge HMC5883L Compass Module
  GY271-B4 = Boladge HMC5883L Compass Module
  GY271-B3 = Boladge HMC5883L Compass Module
  GY271-T3 = Boladge HMC5883L Compass Module
  CON1 = female pin header, 4 pins [form="♀ (female)"]
  Left-Right = female pin header, 3 pins [form="♀ (female)"]
  GY271-T4 = Boladge HMC5883L Compass Module

nets:
  VCC: VL6180X-B2.VIN, VL6180X-T5.VIN, VL6180X-T1.VIN, VL6180X-B5.VIN, VL6180X-B1.VIN, VL6180X-T2.VIN, GY271-T0.VCC, TCA9548A-T.VCC, TCA9548A-B.VCC, TCA9548A-B.A0, GY271-B0.VCC, GY271-B4.VCC, GY271-B3.VCC, GY271-T3.VCC, CON1.pin2, Left-Right.pin2, GY271-T4.VCC
  GND: VL6180X-B2.GND, VL6180X-T5.GND, VL6180X-T1.GND, VL6180X-B5.GND, VL6180X-B1.GND, VL6180X-T2.GND, GY271-T0.GND, TCA9548A-T.GND, TCA9548A-B.GND, GY271-B0.GND, GY271-B4.GND, GY271-B3.GND, GY271-T3.GND, CON1.pin1, GY271-T4.GND
  N1: VL6180X-B2.SCL, TCA9548A-B.2SCL
  N2: VL6180X-B2.SDA, TCA9548A-B.2SDA
  N3: VL6180X-T5.SCL, TCA9548A-T.5SCL
  N4: VL6180X-T5.SDA, TCA9548A-T.5SDA
  N5: VL6180X-T1.SCL, TCA9548A-T.1SCL
  N6: VL6180X-T1.SDA, TCA9548A-T.1SDA
  N7: VL6180X-B5.SCL, TCA9548A-B.5SCL
  N8: VL6180X-B5.SDA, TCA9548A-B.5SDA
  N9: VL6180X-B1.SCL, TCA9548A-B.1SCL
  N10: VL6180X-B1.SDA, TCA9548A-B.1SDA
  N11: VL6180X-T2.SCL, TCA9548A-T.2SCL
  N12: VL6180X-T2.SDA, TCA9548A-T.2SDA
  N13: GY271-T0.SCL, TCA9548A-T.0SCL
  N14: GY271-T0.SDA, TCA9548A-T.0SDA
  N15: TCA9548A-T.3SDA, GY271-T3.SDA
  N16: TCA9548A-T.3SCL, GY271-T3.SCL
  N17: TCA9548A-T.4SDA, GY271-T4.SDA
  N18: TCA9548A-T.4SCL, GY271-T4.SCL
  N19: TCA9548A-T.INPUTSDA, TCA9548A-B.INPUTSDA, CON1.pin3
  N20: TCA9548A-T.INPUTSCL, TCA9548A-B.INPUTSCL, CON1.pin4
  N21: TCA9548A-T.A2, TCA9548A-B.A2, Left-Right.pin3
  N22: TCA9548A-B.3SDA, GY271-B3.SDA
  N23: TCA9548A-B.3SCL, GY271-B3.SCL
  N24: TCA9548A-B.4SDA, GY271-B4.SDA
  N25: TCA9548A-B.4SCL, GY271-B4.SCL
  N26: TCA9548A-B.0SDA, GY271-B0.SDA
  N27: TCA9548A-B.0SCL, GY271-B0.SCL

notes:
  GND
  +5V
  SDA
  SCL

custom parts:
  Adafruit VL6180X Time of Flight Distance Sensor: The VL6180X is a Time of Flight distance sensor like no other you've used! The sensor contains a very tiny invisible laser source, and a matching sensor. The VL6180X can detect the "time of flight", or how long the light has taken to bounce back to the sensor. Since it uses a very narrow light source, it is good for determining distance of only the surface directly in front of it. Unlike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
  Boladge HMC5883L Compass Module: Cheap digital compass module
  Adafruit TCA9548A: You just found the perfect I2C sensor, and you want to wire up two or three or more of them to your Arduino when you realize "Uh oh, this chip has a fixed I2C address, and from what I know about I2C, you cannot have two devices with the same address on the same SDA/SCL pins!" Are you out of luck? You would be, if you didn't have this ultra-cool TCA9548A 1-to-8 I2C multiplexer! Finally, a way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
